# Fritzing sketch raspberrypi-zero-bridge (saved by Fritzing 0.9.2b)
circuit board: 6.5cm x 3.2cm
breadboards: 1

parts:
  U1 = LED CUBE PINOUT [package=ledcube]
  Raspberry_PI = double row rounded female pin header, 40 pins [form="♀ (female rounded)"]

nets:
  N1: U1.LAYER_8, Raspberry_PI.pin20
  N2: U1.CLOCK, Raspberry_PI.pin29
  N3: U1.LAYER_7, Raspberry_PI.pin19
  N4: U1.LAYER_6, Raspberry_PI.pin18
  N5: U1.ENABLE, Raspberry_PI.pin33
  N6: U1.LAYER_5, Raspberry_PI.pin26
  N7: U1.LATCH, Raspberry_PI.pin12
  N8: U1.LAYER_4, Raspberry_PI.pin25
  N9: U1.LAYER_3, Raspberry_PI.pin24
  N10: U1.LAYER_2, Raspberry_PI.pin23
  N11: U1.LAYER_1, Raspberry_PI.pin22
  N12: U1.GND, Raspberry_PI.pin36
  N13: U1.5V, Raspberry_PI.pin1
  N14: U1.BLUE, Raspberry_PI.pin31

notes:
  v1.0
  Raspberry Pi Zero bridge by Fz
